// Digital circuit CPU.dig as structural Verilog
module CPU (
  input  CLK_RAW,
  output [31:0] x8_s0_fp,
  output [31:0] x9_s1,
  output [31:0] x10_a0,
  output [31:0] PC,
  output [31:0] ADDR,
  output [31:0] Instr,
  output [7:0] Dout,
  output [5:0] Step,
  output [7:0] Substep,
  output [7:0] Dval,
  output [16:0] out_11,
  output [15:0] out_12,
  output [31:0] A,
  output [31:0] B,
  output [31:0] Result,
  output [11:0] CSR_Address,
  output [31:0] x11_a1,
  output [31:0] x4_tp,
  output [31:0] x5_t0,
  output [31:0] x6_t1,
  output [31:0] x7_t2,
  output [31:0] x1_ra,
  output [31:0] x2_sp,
  output [31:0] x3_gp,
  output [31:0] x12_a2,
  output [31:0] x13_a3,
  output [31:0] x14_a4,
  output [31:0] x15_a5,
  output [5:0] out_30,
  output [31:0] out_31,
  output [31:0] out_32,
  output [31:0] out_33,
  output [31:0] out_34,
  output [31:0] out_35,
  output [31:0] out_36,
  output [10:0] out_37
);

  wire ADDR_CLK, ADDR_IN, ADDR_LATCH, ALU_A, ALU_AUX, ALU_B, ALU_N, alu_shift_step_1_nsh_output,
       alu_shift_step_1_sh_loadlen, alu_shift_step_1_sh_reset, and_1_out, and_2_out, and_3_out, B_INSTR,
       B_RUN, B_STEP, B_STOP, B_SUBSTEP, BUS_CLK, BUS_EN, BUT_STOP, button_1_out, button_2_out, CLK,
       clock_1_lastsubstep, comparator_1_eq, comparator_1_gt, comparator_1_lt, CSR_ADDR_LATCH, CSR_IN,
       CSR_IN_LATCH, CSR_OUT, CSR_OUT_LATCH, CSR_PC_OUT, d_ff_1_q, d_ff_3_q, diodeforward_1_out, ImmB,
       ImmCSR, ImmI, ImmJ, ImmS, ImmU, INT1P, INT2P, INT3P, IRQ_LATCH, LASTSTEP, LEN8, MEM_IN, MEM_OUT,
       MEPC_OUT, MIE, mie_1_mei1e, mie_1_mei2e, mie_1_mei3e, mip_1_mei1p, mip_1_mei2p, mip_1_mei3p, MRET,
       MTVEC_OUT, multiplexer_1_out, nADDR_PE, nALU_RESET, nCLK, nILL_OP, nIRQ, nKB_INT, nMEM_OE, nMEM_WE,
       nOPDONE, not_1_out, not_2_out, not_3_out, nPC_CNT_PE, nREG_IN_EN, nRESET, nS_EXT, nSTEPDONE, nWAKEUP,
       OP_IMM_LATCH, OP_IN, OP_IN_MUX, OP_LATCH, or_1_out, PC_IN, PC_IN_LATCH, PC_IN_MUX, PC_OUT,
       PC_OUT_LATCH, PC_OUT_SnP, REG_IN, RESET, ROM_SEL, RS1, Running, SLEEP, TRAP_OP, TRAP_OP_SnP;
  wire [0:0] LEN;
  wire [1:0] ALU_A_MUX, REG_IN_MUX, TRAP2;
  wire [2:0] ALU_B_MUX, ALU_OP;
  wire [3:0] RSA, RSB, RSD;
  wire [7:0] ROM_DATA, ROM_DIN;
  wire [15:0] ROM_ADDR;
  wire [31:29] MicroCode_d;

  D_FF_AS #(.Default(1)) d_ff_as_1 (.Set(CLK), .D(1'b0), .C(PC_IN_MUX), .Clr(1'b0), .Q(IRQ_LATCH));  // open: nQ
  Register_view register_view_1 (
    .BUS_CLK(BUS_CLK), .nREG_IN_EN(nREG_IN_EN), .REG_IN(REG_IN), .RSD(RSD), .x1_ra(x1_ra), .x2_sp(x2_sp),
    .x3_gp(x3_gp), .x4_tp(x4_tp), .x5_t0(x5_t0), .x6_t1(x6_t1), .x7_t2(x7_t2), .x8_s0_fp(x8_s0_fp),
    .x9_s1(x9_s1), .x10_a0(x10_a0), .x11_a1(x11_a1), .x12_a2(x12_a2), .x13_a3(x13_a3), .x14_a4(x14_a4),
    .x15_a5(x15_a5));
  not not_1 (not_1_out, MRET);
  Button #(.activeLow("true")) button_1 (.out(button_1_out));
  Button #(.activeLow("true")) button_2 (.out(button_2_out));
  Multiplexer multiplexer_1 (.sel(out_11[13]), .in_0(RS1), .in_1(ImmCSR), .out(multiplexer_1_out));
  PullDown pulldown_1 (.out(CSR_IN));
  and and_1 (and_1_out, not_1_out, PC_IN_MUX);
  Comparator #(.Bits(32)) comparator_1 (
    .a(x3_gp), .b(32'h1), .gt(comparator_1_gt), .eq(comparator_1_eq), .lt(comparator_1_lt));
  LED led_1 (.in(Running));
  LED led_2 (.in(not_2_out));
  not not_2 (not_2_out, Running);
  Button #(.activeLow("true")) Stop (.out(BUT_STOP));
  Button #(.activeLow("true")) Run (.out(B_RUN));
  Button #(.activeLow("true")) One_Instruction (.out(B_INSTR));
  Button #(.activeLow("true")) One_Step (.out(B_STEP));
  Button #(.activeLow("true")) One_Substep (.out(B_SUBSTEP));
  LED led_3 (.in(comparator_1_gt));
  LED led_4 (.in(comparator_1_eq));
  and and_2 (and_2_out, nIRQ, nILL_OP);
  MEPC mepc_1 (
    .BUS_CLK(BUS_CLK), .PC_IN(PC_OUT), .IN_EN(and_1_out), .CSR_IN(CSR_OUT), .CSR_IN_LATCH(CSR_IN_LATCH),
    .CSR_ADDR(CSR_Address), .RESET(RESET), .OUT(MEPC_OUT), .CSR_OUT(CSR_IN), .mepc(out_31));
  MTVEC mtvec_1 (
    .BUS_CLK(BUS_CLK), .MTVEC_SnP(PC_IN_MUX), .CSR_IN_LATCH(CSR_IN_LATCH), .CSR_ADDR(CSR_Address),
    .nRESET(nRESET), .MTVEC_OUT(MTVEC_OUT), .CSR_OUT(CSR_IN));
  MSCRATCH mscratch_1 (
    .BUS_CLK(BUS_CLK), .CSR_IN(CSR_OUT), .CSR_IN_LATCH(CSR_IN_LATCH), .CSR_ADDR(CSR_Address), .RESET(RESET),
    .CSR_OUT(CSR_IN), .mscratch(out_32));
  MSTATUS mstatus_1 (
    .CLK(CLK), .BUS_CLK(BUS_CLK), .CSR_IN(CSR_OUT), .CSR_IN_LATCH(CSR_IN_LATCH),
    .CSR_OUT_LATCH(CSR_OUT_LATCH), .CSR_ADDR(CSR_Address), .IRQ(PC_IN_MUX), .MRET(MRET),
    .IRQ_LATCH(IRQ_LATCH), .RESET(RESET), .nRESET(nRESET), .CSR_OUT(CSR_IN), .mstatus(out_33), .MIE(MIE));  // open: MPIE
  MIE mie_1 (
    .CLK(CLK), .BUS_CLK(BUS_CLK), .CSR_IN(CSR_OUT), .CSR_IN_LATCH(CSR_IN_LATCH),
    .CSR_OUT_LATCH(CSR_OUT_LATCH), .CSR_ADDR(CSR_Address), .nRESET(nRESET), .CSR_OUT(CSR_IN), .mie(out_34),
    .MEI1E(mie_1_mei1e), .MEI2E(mie_1_mei2e), .MEI3E(mie_1_mei3e));
  MIP mip_1 (
    .CLK(CLK), .BUS_CLK(BUS_CLK), .CSR_IN(CSR_OUT), .CSR_IN_LATCH(CSR_IN_LATCH),
    .CSR_OUT_LATCH(CSR_OUT_LATCH), .CSR_ADDR(CSR_Address), .nINT1(nKB_INT), .nINT2(button_1_out),
    .nINT3(button_2_out), .nRESET(nRESET), .CSR_OUT(CSR_IN), .mip(out_35), .MEI1P(mip_1_mei1p),
    .MEI2P(mip_1_mei2p), .MEI3P(mip_1_mei3p));
  MCAUSE mcause_1 (
    .BUS_CLK(BUS_CLK), .CSR_IN_LATCH(CSR_IN_LATCH), .CSR_OUT_LATCH(CSR_OUT_LATCH), .CSR_ADDR(CSR_Address),
    .TRAP2(TRAP2), .nIRQ(nIRQ), .INT1P(INT1P), .INT2P(INT2P), .INT3P(INT3P), .IRQ_LATCH(IRQ_LATCH),
    .nRESET(nRESET), .CSR_OUT(CSR_IN), .mcause(out_36));
  and and_3 (and_3_out, nRESET, nOPDONE);
  CSR csr_1 (
    .CLK(BUS_CLK), .INA(multiplexer_1_out), .INB(CSR_IN), .CSR_FUNC(out_11[12:11]), .ADDR_IN(ImmI),
    .ADDR_LATCH(CSR_ADDR_LATCH), .nRESET(nRESET), .NEW_VAL(CSR_OUT), .ADDR(CSR_Address));
  Interrupt_Controller interrupt_controller_1 (
    .BUS_CLK(BUS_CLK), .IRQ_OP_SnP(TRAP_OP_SnP), .LASTSTEP(LASTSTEP), .nIRQ(and_2_out), .OP_LATCH(OP_LATCH),
    .nRESET(nRESET), .IRQ_OP(TRAP_OP), .IRQ_OP_FETCH(OP_IN_MUX));
  D_FF #(.Default(1)) d_ff_1 (.D(comparator_1_lt), .C(~nOPDONE), .Q(d_ff_1_q));  // open: nQ
  and and_4 (B_STOP, d_ff_1_q, BUT_STOP);
  DebugShift32 debugshift32_1 (.CLK(BUS_CLK), .D(ALU_A), .nEN(1'b0), .Val(A));
  DebugShift32 debugshift32_2 (.CLK(BUS_CLK), .D(ALU_B), .nEN(1'b0), .Val(B));
  DebugShift32 debugshift32_3 (.CLK(BUS_CLK), .D(ADDR_IN), .nEN(1'b0), .Val(Result));
  D_FF_AS d_ff_as_2 (.Set(~1'b1), .D(1'b1), .C(ADDR_LATCH), .Clr(~and_3_out), .Q(TRAP_OP_SnP));  // open: nQ
  not not_3 (not_3_out, TRAP2[0]);
  and and_5 (INT1P, mie_1_mei1e, mip_1_mei1p);
  and and_6 (INT2P, mie_1_mei2e, mip_1_mei2p);
  and and_7 (INT3P, mie_1_mei3e, mip_1_mei3p);
  and and_8 (MRET, not_3_out, TRAP2[1]);
  Reset reset_1 (.out(nRESET));
  Reset #(.invertOutput("false")) reset_2 (.out(RESET));
  Multiplexer multiplexer_2 (.sel(MRET), .in_0(MTVEC_OUT), .in_1(MEPC_OUT), .out(CSR_PC_OUT));
  Multiplexer multiplexer_3 (.sel(PC_IN_MUX), .in_0(ADDR_IN), .in_1(CSR_PC_OUT), .out(PC_IN));
  not not_4 (nPC_CNT_PE, PC_IN_LATCH);
  Multiplexer multiplexer_4 (.sel(OP_IN_MUX), .in_0(MEM_OUT), .in_1(TRAP_OP), .out(OP_IN));
  D_FF d_ff_2 (.D(OP_LATCH), .C(CLK), .Q(OP_IMM_LATCH));  // open: nQ
  Multiplexer #(.Selector_Bits(2)) multiplexer_5 (
    .sel(ALU_A_MUX), .in_0(RS1), .in_1(PC_OUT), .in_2(1'b1), .in_3(1'b0), .out(ALU_A));
  D_FF d_ff_3 (.D(ALU_AUX), .C(CLK), .Q(d_ff_3_q));  // open: nQ
  DiodeForward diodeforward_1 (.in(INT1P), .out(diodeforward_1_out));
  DiodeForward diodeforward_2 (.in(INT2P), .out(diodeforward_1_out));
  DiodeForward diodeforward_3 (.in(INT3P), .out(diodeforward_1_out));
  // Clock_driver clock_driver_1: pin names not known; wires that end beside it: CLK_RAW, B_STOP, B_RUN, B_INSTR, B_STEP, B_SUBSTEP, nSTEPDONE, nOPDONE, nRESET, nWAKEUP, SLEEP, CLK, nCLK, Running
  or or_1 (or_1_out, nSTEPDONE, d_ff_3_q);
  not not_5 (nWAKEUP, diodeforward_1_out);
  PullDown pulldown_2 (.out(diodeforward_1_out));
  nand nand_1 (LEN8, LEN[0], BUS_EN);
  nand nand_2 (nIRQ, MIE, diodeforward_1_out);
  ALU_shift_step alu_shift_step_1 (
    .nCLK(nCLK), .nRESET(nALU_RESET), .nEN(or_1_out), .SH_LOADLEN(alu_shift_step_1_sh_loadlen),
    .nSH_OUTPUT(alu_shift_step_1_nsh_output), .SH_RESET(alu_shift_step_1_sh_reset));
  PC pc_1 (
    .CLK(CLK), .BUS_CLK(BUS_CLK), .IN(PC_IN), .LATCH_IN(PC_IN_LATCH), .LATCH_OUT(PC_OUT_LATCH),
    .SnP_OUT(PC_OUT_SnP), .nPE_CNT(nPC_CNT_PE), .EN_CNT(OP_LATCH), .nRESET(nRESET), .OUT(PC_OUT), .PC(PC));
  and and_9 (PC_OUT_LATCH, nILL_OP, LASTSTEP);
  // OpCode opcode_1: pin names not known; wires that end beside it: BUS_CLK, OP_IN, OP_LATCH, OP_IMM_LATCH, BUS_EN, nRESET, ImmI, ImmS, ImmB, ImmU, ImmJ, ImmCSR, RSA, RSB, RSD, out_11[10:6], out_11[13:11], out_11[14], nS_EXT, out_11[16], TRAP2, Instr, out_12
  Multiplexer #(.Selector_Bits(3)) multiplexer_6 (
    .sel(ALU_B_MUX), .in_0(MEM_IN), .in_1(ImmI), .in_2(ImmS), .in_3(ImmB), .in_4(ImmU), .in_5(ImmJ),
    .in_6(1'b1), .in_7(1'b0), .out(ALU_B));
  nor nor_1 (LASTSTEP, LEN[0], BUS_EN);
  Clock clock_1 (
    .CLK(CLK), .nCLK(nCLK), .nLEN4(LEN8), .LASTSTEP(LASTSTEP), .SUBSTEP_EN(nRESET), .STEP(out_11[5:0]),
    .LASTSUBSTEP(clock_1_lastsubstep), .nSTEPDONE(nSTEPDONE), .SUBSTEP(Substep), .nOPDONE(nOPDONE));  // open: nRESET
  ALU alu_1 (
    .CLK(BUS_CLK), .A(ALU_A), .B(ALU_B), .N(ALU_N), .nRESET_ALU(nALU_RESET), .CLK_F(ALU_AUX), .S(ALU_OP),
    .LOADLEN_SH(alu_shift_step_1_sh_loadlen), .nOUTPUT_SH(alu_shift_step_1_nsh_output),
    .RESET_SH(alu_shift_step_1_sh_reset), .FLAG(out_11[15]), .OUT(ADDR_IN), .DLEN(out_30));  // open: DSUM, C
  Multiplexer #(.Selector_Bits(2)) multiplexer_7 (
    .sel(REG_IN_MUX), .in_0(ADDR_IN), .in_1(MEM_OUT), .in_2(CSR_IN), .in_3(PC_OUT), .out(REG_IN));
  and and_10 (BUS_CLK, CLK, BUS_EN);
  // Mem mem_1: pin names not known; wires that end beside it: CLK, BUS_CLK, MEM_IN, ADDR_IN, ADDR_LATCH, ADDR_CLK, nADDR_PE, nMEM_OE, nMEM_WE, nRESET, ROM_DATA, nS_EXT, MEM_OUT, ADDR, Dout, Dval, ROM_ADDR, ROM_SEL, ROM_DIN, nKB_INT
  Register_bank register_bank_1 (
    .CLK(BUS_CLK), .IN(REG_IN), .nEN_IN(nREG_IN_EN), .SA(RSA), .SB(RSB), .SD(RSD), .RESET(RESET), .A(RS1),
    .B(MEM_IN));
  ROM #(.AddrBits(17), .isProgramMemory("true"), .Bits(32)) MicroCode (
    .A(out_11), .sel(1'b1),
    .D({MicroCode_d, SLEEP, PC_IN_MUX, CSR_IN_LATCH, CSR_OUT_LATCH, CSR_ADDR_LATCH, OP_LATCH, REG_IN_MUX, ALU_B_MUX, ALU_A_MUX, nMEM_WE, nMEM_OE, nADDR_PE, ADDR_CLK, ADDR_LATCH, PC_OUT_SnP, PC_IN_LATCH, nREG_IN_EN, BUS_EN, LEN[0], ALU_OP, ALU_AUX, nALU_RESET, ALU_N}));
  EEPROM #(.AddrBits(16), .Bits(8)) Firmware (.A(ROM_ADDR), .CS(ROM_SEL), .WE(~nMEM_WE), .OE(~nMEM_OE), .D(ROM_DATA));
  assign ROM_DATA = ~nMEM_WE ? ROM_DIN : 8'bz;  // DriverInvSel driverinvsel_1
  D_FF #(.Default(1)) d_ff_4 (.D(MicroCode_d[29]), .C(CLK), .Q(nILL_OP));  // open: nQ

  assign out_37 = out_11[16:6];
  assign Step = out_11[5:0];

  // Other names for the same wires on the sheet: IMM_SnP = BUS_EN; LEN[1] = BUS_EN; PC_CNT_EN = OP_LATCH;
  //   ALU_OUT = ADDR_IN; CSR_ADDR[11:0] = CSR_Address; FLAG = out_11[15]; FUNC3[2:0] = out_11[13:11];
  //   gp[31:0] = x3_gp; Mem_Dout[7:0] = Dout; Mem_Dval[7:0] = Dval; OPCODE[4:0] = out_11[10:6]; RS2 = MEM_IN;
  //   SA = out_11[14]; SYS = out_11[16]

  // Notes on the sheet:
  //   CLK_RAW: Hz: 5000
  //   Debug
  //   Interrupts
  //   CSR
  //   Clock
  //   ALU
  //   PC
  //   Opcode
  //   Registers
  //   Memory
  //   Microcode
  //   ROM
  //   contents of MicroCode (hex, n*v repeats v):
  //   1d1c0a8a,190202,130202,1d0242,170202,1d0242,170202,1d0242,170202,1d0242,3d0202,1d0200,
  //   41c0282,190202,130202,201d0042,201d0042,201d0042,201d0042,201d0102,0,0,0,0,0,0,0,
  //   0,0,0,0,0,1d1c0a8a,190202,130202,1d0242,170202,1d0242,170202,1d0242,170202,1d0242,
  //   3d0202,3d0202,3d0202,3d0302,0,0,0,0,0,0,0,0,0,0,0,0,0,0,0,0,0,0,1d1c0a8a,190202,130202,
  //   1d0242,170202,1d0242,170202,1d0242,170202,1d0242,3d0202,3d0202,3d0202,3d0302,0,0,
  //   0,0,0,0,0,0,0,0,0,0,0,0,0,0,0,0,1d1c0a8a,190202,130202,1d0242,170202,1d0242,170202,
  //   1d0242,170202,1d0242,3d0202,3d0202,3d0202,3d0302,0,0,0,0,0,0,0,0,0,0,0,0,0,0,0,0,
  //   0,0,1d1c0a8a,190202,130202,1d0242,170202,1d0242,170202,1d0242,170202,1d0242,3d0202,
  //   1d0200,41d0082,1d0302,0,0,0,0,0,0,0,0,0,0,0,0,0,0,0,0,0,0,1d1c0a8a,190202,130202,
  //   1d0242,170202,1d0242,170202,1d0242,170202,1d0242,3d0202,1d0200,111d0882,1d0302,0,
  //   0,0,0,0,0,0,0,0,0,0,0,0,0,0,0,0,0,1d1c0a8a,190202,130202,1d0242,170202,1d0242,170202,
  //   1d0242,170202,1d0242,3d0202,3d0202,3d0202,3d0302,0,0,0,0,0,0,0,0,0,0,0,0,0,0,0,0,
  //   0,0,1d1c0a8a,190202,130202,1d0242,170202,1d0242,170202,1d0242,170202,1d0242,3d0202,
  //   3d0202,3d0202,3d0302,0,0,0,0,0,0,0,0,0,0,0,0,0,0,0,0,0,0,1d1c0a8a,190202,130202,1d0242,
  //   170202,1d0242,170202,1d0242,170202,1d0242,3d0202,1d0200,81c0282,190202,1a0242,c0202,
  //   1c0302,0,0,0,0,0,0,0,0,0,0,0,0,0,0,0,1d1c0a8a,190202,130202,1d0242,170202,1d0242,
  //   170202,1d0242,170202,1d0242,3d0202,3d0202,3d0202,3d0302,0,0,0,0,0,0,0,0,0,0,0,0,0,
  //   0,0,0,0,0,1d1c0a8a,190202,130202,1d0242,170202,1d0242,170202,1d0242,170202,1d0242,
  //   3d0202,3d0202,3d0202,3d0302,0,0,0,0,0,0,0,0,0,0,0,0,0,0,0,0,0,0,1d1c0a8a,190202,130202,
  //   1d0242,170202,1d0242,170202,1d0242,170202,1d0242,3d0202,3d0202,3d0202,3d0302,0,0,
  //   0,0,0,0,0,0,0,0,0,0,0,0,0,0,0,0,1d1c0a8a,190202,130202,1d0242,170202,1d0242,170202,
  //   1d0242,170202,1d0242,3d0202,1d0200,1d0082,1d0302,0,0,0,0,0,0,0,0,0,0,0,0,0,0,0,0,
  //   0,0,1d1c0a8a,190202,130202,1d0242,170202,1d0242,170202,1d0242,170202,1d0242,3d0202,
  //   1d0200,131d0082,1d0302,0,0,0,0,0,0,0,0,0,0,0,0,0,0,0,0,0,0,1d1c0a8a,190202,130202,
  //   1d0242,170202,1d0242,170202,1d0242,170202,1d0242,3d0202,3d0202,3d0202,3d0302,0,0,
  //   0,0,0,0,0,0,0,0,0,0,0,0,0,0,0,0,1d1c0a8a,190202,130202,1d0242,170202,1d0242,170202,
  //   1d0242,170202,1d0242,3d0202,3d0202,3d0202,3d0302,0,0,0,0,0,0,0,0,0,0,0,0,0,0,0,0,
  //   0,0,1d1c0a8a,190202,130202,1d0242,170202,1d0242,170202,1d0242,170202,1d0242,3d0202,
  //   3d0202,3d0202,3d0302,0,0,0,0,0,0,0,0,0,0,0,0,0,0,0,0,0,0,1d1c0a8a,190202,130202,1d0242,
  //   170202,1d0242,170202,1d0242,170202,1d0242,3d0202,3d0202,3d0202,3d0302,0,0,0,0,0,0,
  //   0,0,0,0,0,0,0,0,0,0,0,0,1d1c0a8a,190202,130202,1d0242,170202,1d0242,170202,1d0242,
  //   170202,1d0242,3d0202,3d0202,3d0202,3d0302,0,0,0,0,0,0,0,0,0,0,0,0,0,0,0,0,0,0,1d1c0a8a,
  //   190202,130202,1d0242,170202,1d0242,170202,1d0242,170202,1d0242,3d0202,3d0202,3d0202,
  //   3d0302,0,0,0,0,0,0,0,0,0,0,0,0,0,0,0,0,0,0,1d1c0a8a,190202,130202,1d0242,170202,1d0242,
  //   170202,1d0242,170202,1d0242,3d0202,3d0202,3d0202,3d0302,0,0,0,0,0,0,0,0,0,0,0,0,0,
  //   0,0,0,0,0,1d1c0a8a,190202,130202,1d0242,170202,1d0242,170202,1d0242,170202,1d0242,
  //   3d0202,3d0202,3d0202,3d0302,0,0,0,0,0,0,0,0,0,0,0,0,0,0,0,0,0,0,1d1c0a8a,190202,130202,
  //   1d0242,170202,1d0242,170202,1d0242,170202,1d0242,3d0202,3d0202,3d0202,3d0302,0,0,
  //   0,0,0,0,0,0,0,0,0,0,0,0,0,0,0,0,1d1c0a8a,190202,130202,1d0242,170202,1d0242,170202,
  //   1d0242,170202,1d0242,3d0202,3d0202,3d0202,3d0302,0,0,0,0,0,0,0,0,0,0,0,0,0,0,0,0,
  //   0,0,1d1c0a8a,190202,130202,1d0242,170202,1d0242,170202,1d0242,170202,1d0242,3d0202,
  //   1d0201,1d0293,1d0206,1d0302,0,0,0,0,0,0,0,0,0,0,0,0,0,0,0,0,0,1d1c0a8a,190202,130202,
  //   1d0242,170202,1d0242,170202,1d0242,170202,1d0242,3d0202,1d0200,41d0282,1d0600,1d1d08c2,
  //   1d1d0202,191d08c2,191d08c2,191d08c2,191d0842,191d0842,191d0842,1d0302,0,0,0,0,0,0,
  //   0,0,0,1d1c0a8a,190202,130202,1d0242,170202,1d0242,170202,1d0242,170202,1d0242,3d0202,
  //   3d0202,3d0202,3d0302,0,0,0,0,0,0,0,0,0,0,0,0,0,0,0,0,0,0,1d1c0a8a,190202,130202,1d0242,
  //   170202,1d0242,170202,1d0242,170202,1d0242,3d0202,1d0200,151d0a82,1d0600,1d1d08c2,
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  //   contents of Firmware (hex, n*v repeats v):
  //   13,0,0,0,13,0,0,0,13,0,0,0,73,10,0,c0,93,0,f0,ff,73,a0,40,30,f3,22,40,30,73,22,0,
  //   30,73,22,0,30,37,a3,a5,a5,13,3,53,5a,73,0,0,0,73,22,0,30,93,1,10,0,6f,0,0,0,0,0,0,
  //   0,0,0,0,0,0,0,0,0,0,0,0,0,0,0,0,0,0,0,0,0,0,0,0,0,0,0,0,0,0,0,0,0,0,0,0,0,0,0,0,0,
  //   0,0,0,0,0,0,0,0,0,0,0,0,0,0,0,0,0,0,0,0,0,0,0,0,0,0,0,0,0,0,0,0,0,0,0,0,0,0,0,0,0,
  //   0,0,0,0,0,0,0,0,0,0,0,0,0,0,0,0,0,0,0,0,0,0,0,0,0,0,0,0,0,0,0,0,0,0,0,0,0,0,0,0,0,
  //   0,0,0,0,0,0,0,0,0,0,0,0,0,0,0,0,0,0,0,0,0,0,0,0,0,0,0,0,0,0,0,0,0,0,0,0,0,0,0,0,0,
  //   0,0,0,0,0,0,0,0,0,0,0,0,0,0,0,0,0,0,0,0,0,0,0,0,0,0,0,0,0,0,0,0,0,0,0,0,0,0,0,0,0,
  //   0,0,0,0,0,0,0,0,0,0,0,0,0,0,0,0,0,0,0,0,0,0,0,0,0,0,0,0,0,0,0,0,0,0,0,0,0,0,0,0,0,
  //   0,0,0,0,0,0,0,0,0,0,0,0,0,0,0,0,0,0,0,0,0,0,0,0,0,0,0,0,0,0,0,0,0,0,0,0,0,0,0,0,0,
  //   0,0,0,0,0,0,0,0,0,0,0,0,0,0,0,0,0,0,0,0,0,0,0,0,0,0,0,0,0,0,0,0,0,0,0,0,0,0,0,0,0,
  //   0,0,0,0,0,0,0,0,0,0,0,0,0,0,0,0,0,0,0,0,0,0,0,0,0,0,0,0,0,0,0,0,0,0,0,0,0,0,0,0,0,
  //   0,0,0,0,0,0,0,0,0,0,0,0,0,0,0,0,0,0,0,0,0,0,0,0,0,0,0,0,0,0,0,0,0,0,0,0,0,0,0,0,0,
  //   0,0,0,0,0,0,0,0,0,0,0,0,0,0,0,0,0,0,0,0,0,0,0,0,0,0,0,0,0,0,0,0,0,0,0,0,0,0,0,0,0,
  //   0,0,0,0,0,0,0,0,0,0,0,0,0,0,0,0,0,0,0,0,0,0,0,0,0,0,0,0,0,0,0,0,0,0,0,0,0,0,0,0,0,
  //   0,0,0,0,0,0,0,0,0,0,0,0,0,0,0,0,0,0,0,0,0,0,0,0,0,0,0,0,0,0,0,0,0,0,0,0,0,0,0,0,0,
  //   0,0,0,0,0,0,0,0,0,0,0,0,0,0,0,0,0,0,0,0,0,0,0,0,0,0,0,0,0,0,0,0,0,0,0,0,0,0,0,0,0,
  //   0,0,0,0,0,0,0,0,0,0,0,0,0,0,0,0,0,0,0,0,0,0,0,0,0,0,0,0,0,0,0,0,0,0,0,0,0,0,0,0,0,
  //   0,0,0,0,0,0,0,0,0,0,0,0,0,0,0,0,0,0,0,0,0,0,0,0,0,0,0,0,0,0,0,0,0,0,0,0,0,0,0,0,0,
  //   0,0,0,0,0,0,0,0,0,0,0,0,0,0,0,0,0,0,0,0,0,0,0,0,0,0,0,0,0,0,0,0,0,0,0,0,0,0,0,0,0,
  //   0,0,0,0,0,0,0,0,0,0,0,0,0,0,0,0,0,0,0,0,0,0,0,0,0,0,0,0,0,0,0,0,0,0,0,0,0,0,0,0,0,
  //   0,0,0,0,0,0,0,0,0,0,0,0,0,0,0,0,0,0,0,0,0,0,0,0,0,0,0,0,0,0,0,0,0,0,0,0,0,0,0,0,0,
  //   0,0,0,0,0,0,0,0,0,0,0,0,0,0,0,0,0,0,0,0,0,0,0,0,0,0,0,0,0,0,0,0,0,0,0,0,0,0,0,0,0,
  //   0,0,0,0,0,0,0,0,0,0,0,0,0,0,0,0,0,0,0,0,0,0,0,0,0,0,0,0,0,0,0,0,0,0,0,0,0,0,0,0,0,
  //   0,0,0,0,0,0,0,0,0,0,0,0,0,0,0,0,0,0,0,0,0,0,0,0,0,0,0,0,0,0,0,0,0,0,0,0,0,0,0,0,0,
  //   0,0,0,0,0,0,0,0,0,0,0,0,0,0,0,0,0,0,0,0,0,0,0,0,0,0,0,0,0,0,0,0,0,0,0,0,0,0,0,0,0,
  //   0,0,0,0,0,0,0,0,0,0,0,0,0,0,0,0,0,0,0,0,0,0,0,0,0,0,0,0,0,0,0,0,0,0,0,0,0,0,0,0,0,
  //   0,0,0,0,0,0,0,0,0,0,0,0,0,0,0,0,0,0,0,0,0,0,0,0,0,0,0,0,0,0,0,0,0,0,0,0,0,0,0,0,0,
  //   0,0,0,0,0,0,0,0,0,0,0,0,0,0,0,0,0,0,0,0,0,0,0,0,0,0,0,0,0,0,0,0,0,0,0,0,0,0,0,0,0,
  //   0,0,0,0,0,0,0,0,0,0,0,0,0,0,0,0,0,0,0,0,0,0,0,0,0,0,0,0,0,0,0,0,0,0,0,0,0,0,0,0,0,
  //   0,0,0,0,0,0,0,0,0,0,0,0,0,0,0,0,0,0,0,0,0,0,0,0,0,0,0,0,0,0,0,0,0,0,0,0,0,0,0,0,0,
  //   0,0,0,0,0,0,0,0,0,0,0,0,0,0,0,0,0,0,0,0,0,0,0,0,0,0,0,0,0,0,0,0,0,0,0,0,0,0,0,0,0,
  //   0,0,0,0,0,0,0,0,0,0,0,0,0,0,0,0,0,0,0,0,0,0,0,0,0,0,0,0,0,0,0,0,0,0,0,0,0,0,0,0,0,
  //   0,0,0,0,0,0,0,0,0,0,0,0,0,0,0,0,0,0,0,0,0,0,0,0,0,0,0,0,0,0,0,0,0,0,0,0,0,0,0,0,0,
  //   0,0,0,0,0,0,0,0,0,0,0,0,0,0,0,0,0,0,0,0,0,0,0,0,0,0,0,0,0,0,0,0,0,0,0,0,0,0,0,0,0,
  //   0,0,0,0,0,0,0,0,0,0,0,0,0,0,0,0,0,0,0,0,0,0,0,0,0,0,0,0,0,0,0,0,0,0,0,0,0,0,0,0,0,
  //   0,0,0,0,0,0,0,0,0,0,0,0,0,0,0,0,0,0,0,0,0,0,0,0,0,0,0,0,0,0,0,0,0,0,0,0,0,0,0,0,0,
  //   0,0,0,0,0,0,0,0,0,0,0,0,0,0,0,0,0,0,0,0,0,0,0,0,0,0,0,0,0,0,0,0,0,0,0,0,0,0,0,0,0,
  //   0,0,0,0,0,0,0,0,0,0,0,0,0,0,0,0,0,0,0,0,0,0,0,0,0,0,0,0,0,0,0,0,0,0,0,0,0,0,0,0,0,
  //   0,0,0,0,0,0,0,0,0,0,0,0,0,0,0,0,0,0,0,0,0,0,0,0,0,0,0,0,0,0,0,0,0,0,0,0,0,0,0,0,0,
  //   0,0,0,0,0,0,0,0,0,0,0,0,0,0,0,0,0,0,0,0,0,0,0,0,0,0,0,0,0,0,0,0,0,0,0,0,0,0,0,0,0,
  //   0,0,0,0,0,0,0,0,0,0,0,0,0,0,0,0,0,0,0,0,0,0,0,0,0,0,0,0,0,0,0,0,0,0,0,0,0,0,0,0,0,
  //   0,0,0,0,0,0,0,0,0,0,0,0,0,0,0,0,0,0,0,0,0,0,0,0,0,0,0,0,0,0,0,0,0,0,0,0,0,0,0,0,0,
  //   0,0,0,0,0,0,0,0,0,0,0,0,0,0,0,0,0,0,0,0,0,0,0,0,0,0,0,0,0,0,0,0,0,0,0,0,0,0,0,0,0,
  //   0,0,0,0,0,0,0,0,0,0,0,0,0,0,0,0,0,0,0,0,0,0,0,0,0,0,0,0,0,0,0,0,0,0,0,0,0,0,0,0,0,
  //   0,0,0,0,0,0,0,0,0,0,0,0,0,0,0,0,0,0,0,0,0,0,0,0,0,0,0,0,0,0,0,0,0,0,0,0,0,0,0,0,0,
  //   0,0,0,0,0,0,0,0,0,0,0,0,0,0,0,0,0,0,0,0,0,0,0,0,0,0,0,0,0,0,0,0,0,0,0,0,0,0,0,0,0,
  //   0,0,0,0,0,0,0,0,0,0,0,0,0,0,0,0,0,0,0,0,0,0,0,0,0,0,0,0,0,0,0,0,0,0,0,0,0,0,0,0,0,
  //   0,0,0,0,0,0,0,0,0,0,0,0,0,0,0,0,0,0,0,0,0,0,0,0,0,0,0,0,0,0,0,0,0,0,0,0,0,0,0,0,0,
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endmodule
